// Logisim project P0_L0_CRC.circ as structural Verilog: 2 circuits, main circuit CRC
module CRC (
  input  [7:0] in_1,
  input  [3:0] in_2,
  output [10:0] C
);

  wire [2:0] div_4_1_c, div_4_2_c, div_4_3_c, div_4_4_c, div_4_5_c, div_4_6_c, div_4_7_c;
  wire [10:0] A_extend, bit_extender_1_out;

  assign bit_extender_1_out = {{3{1'b0}}, in_1};  // Bit_Extender bit_extender_1
  Shifter #(.width(11)) shifter_1 (.in(bit_extender_1_out), .\dist (4'b0011), .out(A_extend));
  Div_4 div_4_1 (.A(A_extend[10:7]), .B(in_2), .C(div_4_1_c));  // open: D
  Div_4 div_4_2 (.A({div_4_1_c, A_extend[6]}), .B(in_2), .C(div_4_2_c));  // open: D
  Div_4 div_4_3 (.A({div_4_2_c, A_extend[5]}), .B(in_2), .C(div_4_3_c));  // open: D
  Div_4 div_4_4 (.A({div_4_3_c, A_extend[4]}), .B(in_2), .C(div_4_4_c));  // open: D
  Div_4 div_4_5 (.A({div_4_4_c, A_extend[3]}), .B(in_2), .C(div_4_5_c));  // open: D
  Div_4 div_4_6 (.A({div_4_5_c, A_extend[2]}), .B(in_2), .C(div_4_6_c));  // open: D
  Div_4 div_4_7 (.A({div_4_6_c, A_extend[1]}), .B(in_2), .C(div_4_7_c));  // open: D
  Div_4 div_4_8 (.A({div_4_7_c, A_extend[0]}), .B(in_2), .C(C[2:0]));  // open: D

  assign C[10:3] = in_1;

  // Other names for the same wires on the sheet: B[3:0] = in_2; E[2:0] = C[2:0]; A[7:0] = in_1
endmodule

module Div_4 (
  input  [3:0] A,
  input  [3:0] B,
  output [2:0] C,
  output D
);

  wire [3:0] multiplexer_1_out, xor_1_out;

  Multiplexer #(.width(4), .enable("false")) multiplexer_1 (
    .in0(4'b0000), .in1(B), .out(multiplexer_1_out), .sel(A[3]));
  assign xor_1_out = multiplexer_1_out ^ A;  // XOR_Gate xor_1, 4 bits wide
  Bit_Extender #(.in_width(4), .out_width(3)) bit_extender_1 (.in(xor_1_out), .out(C));

  assign D = A[3];
endmodule
