// Logisim project P0_L0_FSM.circ as structural Verilog: 3 circuits, main circuit fsm
module fsm (
  input  in_1,
  input  [1:0] in_2,
  output out_3
);

  wire clk, clock_2_out;
  wire [1:0] register_1_q, trans_1_c0_;

  Clock clock_1 (.out(clk));
  trans trans_1 (
    .C1(register_1_q[1]), .C0(register_1_q[0]), .IN1(in_2[1]), .IN0(in_2[0]), .reset(in_1),
    .C1_(trans_1_c0_[1]), .C0_(trans_1_c0_[0]));
  Register #(.width(2)) register_1 (.D(trans_1_c0_), .Q(register_1_q), .clk(clock_2_out));  // open: en, clr
  Clock clock_2 (.out(clock_2_out));
  print print_1 (.C1(register_1_q[1]), .C0(register_1_q[0]), .IN1(in_2[1]), .IN0(in_2[0]), .Z(out_3));

  // Other names for the same wires on the sheet: clr = in_1; in[1:0] = in_2; z = out_3
endmodule

module trans (
  input  C1,
  input  C0,
  input  IN1,
  input  IN0,
  input  reset,
  output C1_,
  output C0_
);

  wire and_2_out, and_3_out, not_1_out, not_2_out, not_3_out, not_4_out, not_5_out, not_6_out, not_7_out,
       not_8_out, not_9_out;

  not not_1 (not_1_out, C1);
  not not_2 (not_2_out, IN0);
  not not_3 (not_3_out, reset);
  not not_4 (not_4_out, C1);
  not not_5 (not_5_out, IN1);
  not not_6 (not_6_out, reset);
  not not_7 (not_7_out, C0);
  not not_8 (not_8_out, IN1);
  not not_9 (not_9_out, reset);
  and and_1 (C1_, not_1_out, C0, not_2_out, not_3_out);
  and and_2 (and_2_out, not_4_out, not_5_out, IN0, not_6_out);
  and and_3 (and_3_out, not_7_out, not_8_out, IN0, not_9_out);
  or or_1 (C0_, and_2_out, and_3_out);
endmodule

module print (
  input  C1,
  input  C0,
  input  IN1,
  input  IN0,
  output Z
);

  wire and_1_out, and_2_out, not_1_out;

  and and_1 (and_1_out, C1, not_1_out);
  not not_1 (not_1_out, IN0);
  and and_2 (and_2_out, C1, C0);
  or or_1 (Z, and_1_out, and_2_out);
endmodule
