// Logisim project P0_L0_GRF.circ as structural Verilog: 1 circuit, main circuit grf
module grf (
  input  in_1,
  input  in_2,
  input  [4:0] in_3,
  input  [4:0] in_4,
  input  [4:0] in_5,
  input  [31:0] in_6,
  output [31:0] out_7,
  output [31:0] out_8
);

  wire clk, decoder_1_out0, decoder_1_out1, decoder_1_out2, decoder_1_out3, decoder_1_out4, decoder_1_out5,
       decoder_1_out6, decoder_1_out7, decoder_1_out8, decoder_1_out9, decoder_1_out10, decoder_1_out11,
       decoder_1_out12, decoder_1_out13, decoder_1_out14, decoder_1_out15, decoder_1_out16, decoder_1_out17,
       decoder_1_out18, decoder_1_out19, decoder_1_out20, decoder_1_out21, decoder_1_out22, decoder_1_out23,
       decoder_1_out24, decoder_1_out25, decoder_1_out26, decoder_1_out27, decoder_1_out28, decoder_1_out29,
       decoder_1_out30, decoder_1_out31, EN0, EN1, EN2, EN3, EN4, EN5, EN6, EN7, EN8, EN9, EN10, EN11, EN12,
       EN13, EN14, EN15, EN16, EN17, EN18, EN19, EN20, EN21, EN22, EN23, EN24, EN25, EN26, EN27, EN28, EN29,
       EN30, EN31;
  wire [31:0] O0, O1, O2, O3, O4, O5, O6, O7, O8, O9, O10, O11, O12, O13, O14, O15, O16, O17, O18, O19, O20,
       O21, O22, O23, O24, O25, O26, O28, O29, O30, O31;

  Clock clock_1 (.out(clk));
  Decoder #(.select(5)) decoder_1 (
    .out0(decoder_1_out0), .out1(decoder_1_out1), .out2(decoder_1_out2), .out3(decoder_1_out3),
    .out4(decoder_1_out4), .out5(decoder_1_out5), .out6(decoder_1_out6), .out7(decoder_1_out7),
    .out8(decoder_1_out8), .out9(decoder_1_out9), .out10(decoder_1_out10), .out11(decoder_1_out11),
    .out12(decoder_1_out12), .out13(decoder_1_out13), .out14(decoder_1_out14), .out15(decoder_1_out15),
    .out16(decoder_1_out16), .out17(decoder_1_out17), .out18(decoder_1_out18), .out19(decoder_1_out19),
    .out20(decoder_1_out20), .out21(decoder_1_out21), .out22(decoder_1_out22), .out23(decoder_1_out23),
    .out24(decoder_1_out24), .out25(decoder_1_out25), .out26(decoder_1_out26), .out27(decoder_1_out27),
    .out28(decoder_1_out28), .out29(decoder_1_out29), .out30(decoder_1_out30), .out31(decoder_1_out31),
    .sel(in_5), .en(in_2));
  and and_1 (EN0, in_2, decoder_1_out0);
  and and_2 (EN1, in_2, decoder_1_out1);
  and and_3 (EN2, in_2, decoder_1_out2);
  and and_4 (EN3, in_2, decoder_1_out3);
  and and_5 (EN4, in_2, decoder_1_out4);
  and and_6 (EN5, in_2, decoder_1_out5);
  and and_7 (EN6, in_2, decoder_1_out6);
  and and_8 (EN7, in_2, decoder_1_out7);
  and and_9 (EN8, in_2, decoder_1_out8);
  and and_10 (EN9, in_2, decoder_1_out9);
  and and_11 (EN10, in_2, decoder_1_out10);
  and and_12 (EN11, in_2, decoder_1_out11);
  and and_13 (EN12, in_2, decoder_1_out12);
  and and_14 (EN13, in_2, decoder_1_out13);
  and and_15 (EN14, in_2, decoder_1_out14);
  and and_16 (EN15, in_2, decoder_1_out15);
  and and_17 (EN16, decoder_1_out16, in_2);
  and and_18 (EN17, decoder_1_out17, in_2);
  and and_19 (EN18, decoder_1_out18, in_2);
  and and_20 (EN19, decoder_1_out19, in_2);
  and and_21 (EN20, decoder_1_out20, in_2);
  and and_22 (EN21, decoder_1_out21, in_2);
  and and_23 (EN22, decoder_1_out22, in_2);
  and and_24 (EN23, decoder_1_out23, in_2);
  and and_25 (EN24, decoder_1_out24, in_2);
  and and_26 (EN25, decoder_1_out25, in_2);
  and and_27 (EN26, decoder_1_out26, in_2);
  and and_28 (EN27, decoder_1_out27, in_2);
  and and_29 (EN28, decoder_1_out28, in_2);
  and and_30 (EN29, decoder_1_out29, in_2);
  and and_31 (EN30, decoder_1_out30, in_2);
  and and_32 (EN31, decoder_1_out31, in_2);
  Register #(.width(32)) register_1 (.D({32{1'b0}}), .en(EN0), .Q(O0), .clk(clk), .clr(in_1));
  Register #(.width(32)) register_2 (.D(in_6), .en(EN8), .Q(O8), .clk(clk), .clr(in_1));
  Register #(.width(32)) register_3 (.D(in_6), .en(EN16), .Q(O16), .clk(clk), .clr(in_1));
  Register #(.width(32)) register_4 (.D(in_6), .en(EN24), .Q(O24), .clk(clk), .clr(in_1));
  Register #(.width(32)) register_5 (.D(in_6), .en(EN1), .Q(O1), .clk(clk), .clr(in_1));
  Register #(.width(32)) register_6 (.D(in_6), .en(EN9), .Q(O9), .clk(clk), .clr(in_1));
  Register #(.width(32)) register_7 (.D(in_6), .en(EN17), .Q(O17), .clk(clk), .clr(in_1));
  Register #(.width(32)) register_8 (.D(in_6), .en(EN25), .Q(O25), .clk(clk), .clr(in_1));
  Register #(.width(32)) register_9 (.D(in_6), .en(EN2), .Q(O2), .clk(clk), .clr(in_1));
  Register #(.width(32)) register_10 (.D(in_6), .en(EN10), .Q(O10), .clk(clk), .clr(in_1));
  Register #(.width(32)) register_11 (.D(in_6), .en(EN18), .Q(O18), .clk(clk), .clr(in_1));
  Register #(.width(32)) register_12 (.D(in_6), .en(EN26), .Q(O26), .clk(clk), .clr(in_1));
  Multiplexer #(.select(5), .width(32)) multiplexer_1 (
    .in0(O0), .in1(O1), .in2(O2), .in3(O3), .in4(O4), .in5(O5), .in6(O6), .in7(O7), .in8(O8), .in9(O9),
    .in10(O10), .in11(O11), .in12(O12), .in13(O13), .in14(O14), .in15(O15), .in16(O16), .in17(O17),
    .in18(O18), .in19(O19), .in20(O20), .in21(O21), .in22(O22), .in23(O23), .in24(O24), .in25(O25),
    .in26(O26), .in27(O26), .in28(O28), .in29(O29), .in30(O30), .in31(O31), .out(out_7), .sel(in_3));  // open: en
  Register #(.width(32)) register_13 (.D(in_6), .en(EN3), .Q(O3), .clk(clk), .clr(in_1));
  Register #(.width(32)) register_14 (.D(in_6), .en(EN11), .Q(O11), .clk(clk), .clr(in_1));
  Register #(.width(32)) register_15 (.D(in_6), .en(EN19), .Q(O19), .clk(clk), .clr(in_1));
  Register #(.width(32)) register_16 (.D(in_6), .en(EN27), .Q(O26), .clk(clk), .clr(in_1));
  Register #(.width(32)) register_17 (.D(in_6), .en(EN4), .Q(O4), .clk(clk), .clr(in_1));
  Register #(.width(32)) register_18 (.D(in_6), .en(EN12), .Q(O12), .clk(clk), .clr(in_1));
  Register #(.width(32)) register_19 (.D(in_6), .en(EN20), .Q(O20), .clk(clk), .clr(in_1));
  Register #(.width(32)) register_20 (.D(in_6), .en(EN28), .Q(O28), .clk(clk), .clr(in_1));
  Register #(.width(32)) register_21 (.D(in_6), .en(EN5), .Q(O5), .clk(clk), .clr(in_1));
  Register #(.width(32)) register_22 (.D(in_6), .en(EN13), .Q(O13), .clk(clk), .clr(in_1));
  Register #(.width(32)) register_23 (.D(in_6), .en(EN21), .Q(O21), .clk(clk), .clr(in_1));
  Register #(.width(32)) register_24 (.D(in_6), .en(EN29), .Q(O29), .clk(clk), .clr(in_1));
  Register #(.width(32)) register_25 (.D(in_6), .en(EN6), .Q(O6), .clk(clk), .clr(in_1));
  Register #(.width(32)) register_26 (.D(in_6), .en(EN14), .Q(O14), .clk(clk), .clr(in_1));
  Register #(.width(32)) register_27 (.D(in_6), .en(EN22), .Q(O22), .clk(clk), .clr(in_1));
  Register #(.width(32)) register_28 (.D(in_6), .en(EN30), .Q(O30), .clk(clk), .clr(in_1));
  Multiplexer #(.select(5), .width(32)) multiplexer_2 (
    .in0(O0), .in1(O1), .in2(O2), .in3(O3), .in4(O4), .in5(O5), .in6(O6), .in7(O7), .in8(O8), .in9(O9),
    .in10(O10), .in11(O11), .in12(O12), .in13(O13), .in14(O14), .in15(O15), .in16(O16), .in17(O17),
    .in18(O18), .in19(O19), .in20(O20), .in21(O21), .in22(O22), .in23(O23), .in24(O24), .in25(O25),
    .in26(O26), .in27(O26), .in28(O28), .in29(O29), .in30(O30), .in31(O31), .out(out_8), .sel(in_4));  // open: en
  Register #(.width(32)) register_29 (.D(in_6), .en(EN7), .Q(O7), .clk(clk), .clr(in_1));
  Register #(.width(32)) register_30 (.D(in_6), .en(EN15), .Q(O15), .clk(clk), .clr(in_1));
  Register #(.width(32)) register_31 (.D(in_6), .en(EN23), .Q(O23), .clk(clk), .clr(in_1));
  Register #(.width(32)) register_32 (.D(in_6), .en(EN31), .Q(O31), .clk(clk), .clr(in_1));

  // Other names for the same wires on the sheet: A1[4:0] = in_3; A2[4:0] = in_4; A3[4:0] = in_5; O27[31:0] = O26;
  //   RD1[31:0] = out_7; RD2[31:0] = out_8; reset = in_1; WD[31:0] = in_6; we = in_2
endmodule
