// Logisim project P0_L1_ftoi.circ as structural Verilog: 5 circuits, main circuit ftoi
module ftoi (
  input  [15:0] in_1,
  output [31:0] out_2
);

  wire Elt0, isDen, isInf, isNaN, isNor, type34;
  wire [4:0] E, minus_E;
  wire [10:10] and_1_out;
  wire [31:0] adder_1_out, bit_extender_1_out, bitneg_1_out_2, multiplexer_1_out, multiplexer_2_out,
       shifter_1_out, shifter_2_out, type12ans;

  and and_1 (and_1_out[10], 1'b1, isNor);
  getType getType (.in_1(in_1[14:10]), .in_2(in_1[9:0]), .isNor(isNor), .isDen(isDen), .isInf(isInf), .isNaN(isNaN));
  getE getE (.in_1(in_1[14:10]), .E(E));
  bitNeg bitneg_1 (.in_1(type12ans), .out_2(bitneg_1_out_2));
  assign bit_extender_1_out = {{21{1'b0}}, {and_1_out[10], in_1[9:0]}};  // Bit_Extender bit_extender_1
  Adder #(.width(32)) adder_1 (.a(bitneg_1_out_2), .b(32'h1), .out(adder_1_out));  // open: cin, cout
  Negator #(.width(5)) negator_1 (.in(E), .out(minus_E));
  Multiplexer #(.width(32), .enable("false")) multiplexer_1 (
    .in0(type12ans), .in1(adder_1_out), .out(multiplexer_1_out), .sel(in_1[15]));
  xor xor_1 (type34, isInf, isNaN);
  Shifter #(.width(32)) shifter_1 (.in(bit_extender_1_out), .\dist (E), .out(shifter_1_out));
  Shifter #(.width(32), .shift("lr")) shifter_2 (.in(bit_extender_1_out), .\dist (minus_E), .out(shifter_2_out));
  Comparator #(.width(5)) comparator_1 (.a(E), .b({5{1'b0}}), .lt(Elt0));  // open: gt, eq
  Multiplexer #(.width(32), .enable("false")) multiplexer_2 (
    .in0(shifter_1_out), .in1(shifter_2_out), .out(multiplexer_2_out), .sel(Elt0));
  Multiplexer #(.width(32), .enable("false")) multiplexer_3 (
    .in0(multiplexer_1_out), .in1({32{1'b0}}), .out(out_2), .sel(type34));
  Shifter #(.width(32), .shift("lr")) shifter_3 (.in(multiplexer_2_out), .\dist (5'b01010), .out(type12ans));

  // Other names for the same wires on the sheet: float[15:0] = in_1; frac[9:0] = in_1[9:0];
  //   exponent[4:0] = in_1[14:10]; S = in_1[15]; int[31:0] = out_2
endmodule

module getType (
  input  [4:0] in_1,
  input  [9:0] in_2,
  output isNor,
  output isDen,
  output isInf,
  output isNaN
);

  wire buffer_1_out, comparator_1_gt, comparator_1_lt, comparator_2_gt, comparator_2_lt, fracIs0, isInOrNaN,
       not0, not31, not_1_out;

  Comparator #(.width(5)) comparator_1 (
    .a(in_1), .b({5{1'b0}}), .gt(comparator_1_gt), .eq(isDen), .lt(comparator_1_lt));
  Comparator #(.width(5), .mode("unsigned")) comparator_2 (
    .a(in_1), .b({5{1'b1}}), .gt(comparator_2_gt), .eq(isInOrNaN), .lt(comparator_2_lt));
  Comparator #(.width(10), .mode("unsigned")) comparator_3 (.a(in_2), .b({10{1'b0}}), .eq(fracIs0));  // open: gt, lt
  not not_1 (not_1_out, fracIs0);
  buf buffer_1 (buffer_1_out, isInOrNaN);
  or or_1 (not0, comparator_1_gt, comparator_1_lt);
  or or_2 (not31, comparator_2_gt, comparator_2_lt);
  and and_1 (isInf, fracIs0, isInOrNaN);
  and and_2 (isNaN, not_1_out, buffer_1_out);
  and and_3 (isNor, not0, not31);

  // Other names for the same wires on the sheet: exponent[4:0] = in_1; frac[9:0] = in_2
endmodule

module getE (
  input  [4:0] in_1,
  output [4:0] E
);

  Subtractor #(.width(5)) subtractor_1 (.a(in_1), .b(5'b01111), .out(E));  // open: bin, bout

  // Other names for the same wires on the sheet: exponent[4:0] = in_1
endmodule

module getM (
  input  [4:0] in_1,
  input  [9:0] in_2
);

  wire comparator_1_eq;

  Comparator #(.width(5)) comparator_1 (.a(in_1), .b({5{1'b0}}), .eq(comparator_1_eq));  // open: gt, lt

  // Other names for the same wires on the sheet: exponent[4:0] = in_1; frac[9:0] = in_2
endmodule

module bitNeg (
  input  [31:0] in_1,
  output [31:0] out_2
);

  not not_1 (out_2[0], in_1[0]);
  not not_2 (out_2[1], in_1[1]);
  not not_3 (out_2[2], in_1[2]);
  not not_4 (out_2[3], in_1[3]);
  not not_5 (out_2[4], in_1[4]);
  not not_6 (out_2[5], in_1[5]);
  not not_7 (out_2[6], in_1[6]);
  not not_8 (out_2[7], in_1[7]);
  not not_9 (out_2[8], in_1[8]);
  not not_10 (out_2[9], in_1[9]);
  not not_11 (out_2[10], in_1[10]);
  not not_12 (out_2[11], in_1[11]);
  not not_13 (out_2[12], in_1[12]);
  not not_14 (out_2[13], in_1[13]);
  not not_15 (out_2[14], in_1[14]);
  not not_16 (out_2[15], in_1[15]);
  not not_17 (out_2[16], in_1[16]);
  not not_18 (out_2[17], in_1[17]);
  not not_19 (out_2[18], in_1[18]);
  not not_20 (out_2[19], in_1[19]);
  not not_21 (out_2[20], in_1[20]);
  not not_22 (out_2[21], in_1[21]);
  not not_23 (out_2[22], in_1[22]);
  not not_24 (out_2[23], in_1[23]);
  not not_25 (out_2[24], in_1[24]);
  not not_26 (out_2[25], in_1[25]);
  not not_27 (out_2[26], in_1[26]);
  not not_28 (out_2[27], in_1[27]);
  not not_29 (out_2[28], in_1[28]);
  not not_30 (out_2[29], in_1[29]);
  not not_31 (out_2[30], in_1[30]);
  not not_32 (out_2[31], in_1[31]);
endmodule
