// Logisim project P0_L1_navigation_2020.circ as structural Verilog: 3 circuits, main circuit navigation
module navigation (
  input  [1:0] dir,
  input  in_2,
  input  in_3,
  output out_4,
  output out_5
);

  wire clk, trans_1_hit;
  wire [2:0] register_2_q, trans_1_c0_;

  Clock clock_1 (.out(clk));
  trans trans_1 (
    .C2(register_2_q[2]), .C1(register_2_q[1]), .C0(register_2_q[0]), .IN1(dir[1]), .IN0(dir[0]),
    .C2_(trans_1_c0_[2]), .C1_(trans_1_c0_[1]), .C0_(trans_1_c0_[0]), .HIT(trans_1_hit));
  Register #(.width(1)) register_1 (.D(trans_1_hit), .Q(out_5), .clk(clk), .clr(in_3));  // open: en
  Register #(.width(3)) register_2 (.D(trans_1_c0_), .Q(register_2_q), .clk(clk), .clr(in_3));  // open: en
  print print_1 (.C2(register_2_q[2]), .C1(register_2_q[1]), .C0(register_2_q[0]), .ARRIVE(out_4));

  // Other names for the same wires on the sheet: arrive = out_4; hit = out_5; reset = in_3
endmodule

module trans (
  input  C2,
  input  C1,
  input  C0,
  input  IN1,
  input  IN0,
  output C2_,
  output C1_,
  output C0_,
  output HIT
);

  wire and_1_out, and_2_out, and_3_out, and_4_out, and_5_out, and_6_out, and_7_out, and_8_out, and_9_out,
       and_10_out, and_11_out, and_12_out, and_13_out, and_14_out, and_15_out, and_16_out, not_1_out,
       not_2_out, not_3_out, not_4_out, not_5_out, not_6_out, not_7_out, not_8_out, not_9_out, not_10_out,
       not_11_out, not_12_out, not_13_out, not_14_out, not_15_out, not_16_out, not_17_out, not_18_out,
       not_19_out, not_20_out, not_21_out, not_22_out, not_23_out, not_24_out, not_25_out, not_26_out,
       not_27_out, not_28_out, not_29_out, not_30_out, not_31_out, not_32_out, not_33_out, not_34_out,
       not_35_out, not_36_out, not_37_out, not_38_out, not_39_out, not_40_out;

  not not_1 (not_1_out, C2);
  not not_2 (not_2_out, C0);
  not not_3 (not_3_out, IN1);
  not not_4 (not_4_out, IN0);
  not not_5 (not_5_out, C2);
  not not_6 (not_6_out, IN1);
  not not_7 (not_7_out, C2);
  not not_8 (not_8_out, C1);
  not not_9 (not_9_out, IN1);
  not not_10 (not_10_out, C2);
  not not_11 (not_11_out, IN1);
  not not_12 (not_12_out, IN0);
  not not_13 (not_13_out, C2);
  not not_14 (not_14_out, C0);
  not not_15 (not_15_out, IN1);
  not not_16 (not_16_out, C2);
  not not_17 (not_17_out, C0);
  not not_18 (not_18_out, IN0);
  not not_19 (not_19_out, C2);
  not not_20 (not_20_out, C2);
  not not_21 (not_21_out, C1);
  not not_22 (not_22_out, IN1);
  not not_23 (not_23_out, IN0);
  not not_24 (not_24_out, C2);
  not not_25 (not_25_out, C2);
  not not_26 (not_26_out, C2);
  not not_27 (not_27_out, IN0);
  not not_28 (not_28_out, C2);
  not not_29 (not_29_out, C0);
  not not_30 (not_30_out, IN1);
  not not_31 (not_31_out, C2);
  not not_32 (not_32_out, C1);
  not not_33 (not_33_out, C0);
  not not_34 (not_34_out, C2);
  not not_35 (not_35_out, C0);
  not not_36 (not_36_out, IN0);
  not not_37 (not_37_out, C2);
  not not_38 (not_38_out, C2);
  not not_39 (not_39_out, IN1);
  not not_40 (not_40_out, IN0);
  and and_1 (and_1_out, not_1_out, C1, not_2_out, not_3_out, not_4_out);
  and and_2 (and_2_out, not_5_out, C1, C0, not_6_out, IN0);
  and and_3 (and_3_out, not_7_out, not_8_out, C0, not_9_out);
  and and_4 (and_4_out, not_10_out, C0, not_11_out, not_12_out);
  and and_5 (and_5_out, not_13_out, C1, not_14_out, not_15_out, IN0);
  and and_6 (and_6_out, not_16_out, C1, not_17_out, IN1, not_18_out);
  and and_7 (and_7_out, not_19_out, C1, C0, IN1, IN0);
  and and_8 (and_8_out, not_20_out, not_21_out, not_22_out, not_23_out);
  and and_9 (and_9_out, not_24_out, C0, IN1, IN0);
  and and_10 (and_10_out, not_25_out, C1, IN1, IN0);
  and and_11 (and_11_out, not_26_out, C1, C0, not_27_out);
  and and_12 (and_12_out, not_28_out, not_29_out, not_30_out, IN0);
  and and_13 (and_13_out, not_31_out, not_32_out, not_33_out, IN1);
  and and_14 (and_14_out, not_34_out, not_35_out, IN1, not_36_out);
  and and_15 (and_15_out, not_37_out, C0, IN1, IN0);
  and and_16 (and_16_out, not_38_out, C1, C0, not_39_out, not_40_out);
  or or_1 (C2_, and_1_out, and_2_out);
  or or_2 (C1_, and_3_out, and_4_out, and_5_out, and_6_out, and_7_out);
  or or_3 (C0_, and_8_out, and_9_out, and_10_out, and_11_out);
  or or_4 (HIT, and_12_out, and_13_out, and_14_out, and_15_out, and_16_out);
endmodule

module print (
  input  C2,
  input  C1,
  input  C0,
  output ARRIVE
);


  assign ARRIVE = C2;
endmodule
