// Logisim project P3_CPU.circ as structural Verilog: 8 circuits, main circuit main
module main (
  input  reset,
  output [31:0] out_2,
  output out_3,
  output [4:0] out_4,
  output [31:0] out_5,
  output out_6,
  output [4:0] out_7,
  output [31:0] out_8
);

  wire ALUSrc, clk, isZero;
  wire [1:0] ExtOp, MemtoReg, nPC_sel, RegDst;
  wire [3:0] ALUctr;
  wire [31:0] alu_1_out_4, dm_1_rd, EXT, GPR_rs, multiplexer_2_out, npc_1_npc, PC_4, register_1_q;

  Clock clock_1 (.out(clk));
  NPC npc_1 (
    .PC(register_1_q), .in_2(out_2[25:0]), .in_3(EXT), .in_4(GPR_rs), .nPC_sel(nPC_sel), .NPC(npc_1_npc),
    .in_6(isZero));
  Multiplexer #(.select(2), .width(5), .enable("false")) multiplexer_1 (
    .in0(out_2[20:16]), .in1(out_2[15:11]), .in2({5{1'b1}}), .out(out_4), .sel(RegDst));  // open: in3
  Register #(.width(32)) register_1 (.D(npc_1_npc), .Q(register_1_q), .clk(clk), .clr(reset));  // open: en
  IM IM (.Instruction(out_2), .PC(register_1_q));
  Adder #(.width(32)) adder_1 (.a(register_1_q), .b(32'h4), .out(PC_4));  // open: cin, cout
  GRF grf_1 (
    .in_3(out_2[25:21]), .in_4(out_2[20:16]), .in_5(out_4), .in_6(out_5), .out_8(GPR_rs), .out_9(out_8),
    .in_7(reset), .in_2(out_3), .in_1(clk));
  Ext ext_1 (.Imm(out_2[15:0]), .ExtOp(ExtOp), .Ext(EXT));
  Multiplexer #(.width(32), .enable("false")) multiplexer_2 (
    .in0(out_8), .in1(EXT), .out(multiplexer_2_out), .sel(ALUSrc));
  Controller controller_1 (
    .opcode(out_2[31:26]), .funct(out_2[5:0]), .out_3(RegDst), .out_4(ALUSrc), .out_5(MemtoReg),
    .out_6(out_3), .out_7(out_6), .out_8(nPC_sel), .out_9(ExtOp), .out_10(ALUctr));
  ALU alu_1 (
    .A(GPR_rs), .B(multiplexer_2_out), .ALUop(ALUctr), .out_4({alu_1_out_4[31:7], out_7, alu_1_out_4[1:0]}),
    .out_5(isZero));
  DM dm_1 (.Addr(out_7), .WD(out_8), .RD(dm_1_rd), .MemWrite(out_6), .reset(reset), .in_1(clk));
  Multiplexer #(.select(2), .width(32), .enable("false")) multiplexer_3 (
    .in0({alu_1_out_4[31:7], out_7, alu_1_out_4[1:0]}), .in1(dm_1_rd), .in2(PC_4), .out(out_5), .sel(MemtoReg));  // open: in3

  // Other names for the same wires on the sheet: MemAddr[4:0] = out_7; funct[5:0] = out_2[5:0];
  //   imm16[15:0] = out_2[15:0]; imm26[25:0] = out_2[25:0]; Instr[31:0] = out_2; shamt[4:0] = out_2[10:6];
  //   rd[4:0] = out_2[15:11]; rt[4:0] = out_2[20:16]; rs[4:0] = out_2[25:21]; op[5:0] = out_2[31:26];
  //   MemData[31:0] = out_8; MemWrite = out_6; RegAddr[4:0] = out_4; RegData[31:0] = out_5; RegWrite = out_3
endmodule

module Controller (
  input  [5:0] opcode,
  input  [5:0] funct,
  output [1:0] out_3,
  output out_4,
  output [1:0] out_5,
  output out_6,
  output out_7,
  output [1:0] out_8,
  output [1:0] out_9,
  output [3:0] out_10
);

  wire _000000_out, add_2_out, add_out, beq_out, j_out, jal_out, jr_2_out, jr_out, lui_out, lw_out,
       not_1_out, not_2_out, not_3_out, not_4_out, not_5_out, not_6_out, not_7_out, not_8_out, not_9_out,
       not_10_out, not_11_out, not_12_out, ori_out, sub_2_out, sub_out, sw_out;

  not not_1 (not_1_out, opcode[4]);
  not not_2 (not_2_out, opcode[5]);
  not not_3 (not_3_out, opcode[3]);
  not not_4 (not_4_out, opcode[2]);
  not not_5 (not_5_out, opcode[1]);
  not not_6 (not_6_out, opcode[0]);
  and _000000 (_000000_out, not_2_out, not_1_out, not_3_out, not_4_out, not_5_out, not_6_out);
  and ori (ori_out, not_2_out, not_1_out, opcode[3], opcode[2], not_5_out, opcode[0]);
  and lw (lw_out, opcode[5], not_1_out, not_3_out, not_4_out, opcode[1], opcode[0]);
  and sw (sw_out, opcode[5], not_1_out, opcode[3], not_4_out, opcode[1], opcode[0]);
  and beq (beq_out, not_2_out, not_1_out, not_3_out, opcode[2], not_5_out, not_6_out);
  and lui (lui_out, not_2_out, not_1_out, opcode[3], opcode[2], opcode[1], opcode[0]);
  and j (j_out, not_2_out, not_1_out, not_3_out, not_4_out, opcode[1], not_6_out);
  and jal (jal_out, not_2_out, not_1_out, not_3_out, not_4_out, opcode[1], opcode[0]);
  not not_7 (not_7_out, funct[4]);
  not not_8 (not_8_out, funct[5]);
  not not_9 (not_9_out, funct[3]);
  not not_10 (not_10_out, funct[2]);
  not not_11 (not_11_out, funct[1]);
  not not_12 (not_12_out, funct[0]);
  and add (add_out, funct[5], not_7_out, not_9_out, not_10_out, not_11_out, not_12_out);
  and sub (sub_out, funct[5], not_7_out, not_9_out, not_10_out, funct[1], not_12_out);
  and jr (jr_out, not_8_out, not_7_out, funct[3], not_10_out, not_11_out, not_12_out);
  buf RegDst1 (out_3[1], jal_out);  // OR_Gate
  and add_2 (add_2_out, add_out, _000000_out);
  and sub_2 (sub_2_out, sub_out, _000000_out);
  and jr_2 (jr_2_out, _000000_out, jr_out);
  or RegDst2 (out_3[0], add_2_out, sub_2_out);
  or ALUSrc (out_4, ori_out, lw_out, sw_out, lui_out);
  buf MemtoReg1 (out_5[1], jal_out);  // OR_Gate
  buf MemtoReg0 (out_5[0], lw_out);  // OR_Gate
  or RegWrite (out_6, add_2_out, sub_2_out, ori_out, lw_out, lui_out);
  buf MemWrite (out_7, sw_out);  // OR_Gate
  or nPC_sel1 (out_8[1], jal_out, jr_2_out, j_out);
  or nPC_sel0 (out_8[0], beq_out, jr_2_out);
  buf ExtOp1 (out_9[1], lui_out);  // OR_Gate
  or ExtOp0 (out_9[0], lw_out, sw_out, beq_out);
  buf ALUctr3 (out_10[3], 1'b0);  // OR_Gate
  buf ALUctr2 (out_10[2], 1'b0);  // OR_Gate
  buf ALUctr1 (out_10[1], ori_out);  // OR_Gate
  or ALUctr0 (out_10[0], sub_2_out, beq_out);

  // Other names for the same wires on the sheet: ALUctr[3:0] = out_10; ALUctr0 = out_10[0]; ALUctr1 = out_10[1];
  //   ALUctr2 = out_10[2]; ALUctr3 = out_10[3]; ALUSrc = out_4; ExtOp[1:0] = out_9; ExtOp0 = out_9[0];
  //   ExtOp1 = out_9[1]; fc0 = funct[0]; fc1 = funct[1]; fc2 = funct[2]; fc3 = funct[3]; fc4 = funct[4];
  //   fc5 = funct[5]; MemtoReg[1:0] = out_5; MemtoReg0 = out_5[0]; MemtoReg1 = out_5[1]; MemWrite = out_7;
  //   nPC_sel[1:0] = out_8; nPC_sel0 = out_8[0]; nPC_sel1 = out_8[1]; op0 = opcode[0]; op1 = opcode[1];
  //   op2 = opcode[2]; op3 = opcode[3]; op4 = opcode[4]; op5 = opcode[5]; RegDst[1:0] = out_3; RegDst2 = out_3[0];
  //   RegDst1 = out_3[1]; RegWrite = out_6
endmodule

module ALU (
  input  [31:0] A,
  input  [31:0] B,
  input  [3:0] ALUop,
  output [31:0] out_4,
  output out_5
);

  wire [31:0] A_B, A_B_t, A_B_t_t, A_B_t_t_t, A_B_t_t_t_t;

  Adder #(.width(32)) adder_1 (.a(A), .b(B), .out(A_B_t));  // open: cin, cout
  Subtractor #(.width(32)) subtractor_1 (.a(A), .b(B), .out(A_B_t_t));  // open: bin, bout
  assign A_B_t_t_t_t = A | B;  // OR_Gate or_1, 32 bits wide
  assign A_B = A & B;  // AND_Gate and_1, 32 bits wide
  assign A_B_t_t_t = A ^ B;  // XOR_Gate xor_1, 32 bits wide
  Multiplexer #(.select(4), .width(32)) multiplexer_1 (
    .in0(A_B_t), .in1(A_B_t_t), .in2(A_B_t_t_t_t), .in3(A_B), .in4(A_B_t_t_t), .out(out_4), .sel(ALUop));  // open: in5, in6, in7, in8, in9, in10, in11, in12, in13, in14, in15, en
  Comparator #(.width(32)) comparator_1 (.a(out_4), .b({32{1'b0}}), .eq(out_5));  // open: gt, lt

  // Other names for the same wires on the sheet: isZero = out_5; Result[31:0] = out_4
endmodule

module IM (
  input  [31:0] PC,
  output [31:0] Instruction
);

  wire PC_0x3000;
  wire [31:0] multiplexer_1_out, subtractor_1_out;

  Comparator #(.width(32)) comparator_1 (.a(PC), .b(32'h3000), .gt(PC_0x3000));  // open: eq, lt
  Subtractor #(.width(32)) subtractor_1 (.a(PC), .b(32'h3000), .out(subtractor_1_out));  // open: bin, bout
  Multiplexer #(.width(32), .enable("false")) multiplexer_1 (
    .in0(PC), .in1(subtractor_1_out), .out(multiplexer_1_out), .sel(PC_0x3000));
  ROM #(.addrWidth(5), .dataWidth(32)) rom_1 (.addr(multiplexer_1_out[6:2]), .data(Instruction));  // open: sel
endmodule

module Ext (
  input  [15:0] Imm,
  input  [1:0] ExtOp,
  output [31:0] Ext
);

  wire [31:0] Sign, Zero;

  assign Zero = {{16{1'b0}}, Imm};  // Bit_Extender bit_extender_1
  assign Sign = {{16{Imm[15]}}, Imm};  // Bit_Extender bit_extender_2
  Multiplexer #(.select(2), .width(32), .enable("false")) multiplexer_1 (
    .in0(Zero), .in1(Sign), .in2({Imm, {16{1'b0}}}), .out(Ext), .sel(ExtOp));  // open: in3

  // Other names for the same wires on the sheet: High[31:16] = Imm
endmodule

module GRF (
  input  in_1,
  input  in_2,
  input  [4:0] in_3,
  input  [4:0] in_4,
  input  [4:0] in_5,
  input  [31:0] in_6,
  input  in_7,
  output [31:0] out_8,
  output [31:0] out_9
);

  wire decoder_1_out0, decoder_1_out1, decoder_1_out2, decoder_1_out3, decoder_1_out4, decoder_1_out5,
       decoder_1_out6, decoder_1_out7, decoder_1_out8, decoder_1_out9, decoder_1_out10, decoder_1_out11,
       decoder_1_out12, decoder_1_out13, decoder_1_out14, decoder_1_out15, decoder_1_out16, decoder_1_out17,
       decoder_1_out18, decoder_1_out19, decoder_1_out20, decoder_1_out21, decoder_1_out22, decoder_1_out23,
       decoder_1_out24, decoder_1_out25, decoder_1_out26, decoder_1_out27, decoder_1_out28, decoder_1_out29,
       decoder_1_out30, decoder_1_out31, EN0, EN1, EN2, EN3, EN4, EN5, EN6, EN7, EN8, EN9, EN10, EN11, EN12,
       EN13, EN14, EN15, EN16, EN17, EN18, EN19, EN20, EN21, EN22, EN23, EN24, EN25, EN26, EN27, EN28, EN29,
       EN30, EN31;
  wire [31:0] O0, O1, O2, O3, O4, O5, O6, O7, O8, O9, O10, O11, O12, O13, O14, O15, O16, O17, O18, O19, O20,
       O21, O22, O23, O24, O25, O26, O27, O28, O29, O30, O31;

  Decoder #(.select(5)) decoder_1 (
    .out0(decoder_1_out0), .out1(decoder_1_out1), .out2(decoder_1_out2), .out3(decoder_1_out3),
    .out4(decoder_1_out4), .out5(decoder_1_out5), .out6(decoder_1_out6), .out7(decoder_1_out7),
    .out8(decoder_1_out8), .out9(decoder_1_out9), .out10(decoder_1_out10), .out11(decoder_1_out11),
    .out12(decoder_1_out12), .out13(decoder_1_out13), .out14(decoder_1_out14), .out15(decoder_1_out15),
    .out16(decoder_1_out16), .out17(decoder_1_out17), .out18(decoder_1_out18), .out19(decoder_1_out19),
    .out20(decoder_1_out20), .out21(decoder_1_out21), .out22(decoder_1_out22), .out23(decoder_1_out23),
    .out24(decoder_1_out24), .out25(decoder_1_out25), .out26(decoder_1_out26), .out27(decoder_1_out27),
    .out28(decoder_1_out28), .out29(decoder_1_out29), .out30(decoder_1_out30), .out31(decoder_1_out31),
    .sel(in_5), .en(in_2));
  and and_1 (EN0, in_2, decoder_1_out0);
  and and_2 (EN1, in_2, decoder_1_out1);
  and and_3 (EN2, in_2, decoder_1_out2);
  and and_4 (EN3, in_2, decoder_1_out3);
  and and_5 (EN4, in_2, decoder_1_out4);
  and and_6 (EN5, in_2, decoder_1_out5);
  and and_7 (EN6, in_2, decoder_1_out6);
  and and_8 (EN7, in_2, decoder_1_out7);
  and and_9 (EN8, in_2, decoder_1_out8);
  and and_10 (EN9, in_2, decoder_1_out9);
  and and_11 (EN10, in_2, decoder_1_out10);
  and and_12 (EN11, in_2, decoder_1_out11);
  and and_13 (EN12, in_2, decoder_1_out12);
  and and_14 (EN13, in_2, decoder_1_out13);
  and and_15 (EN14, in_2, decoder_1_out14);
  and and_16 (EN15, in_2, decoder_1_out15);
  and and_17 (EN16, decoder_1_out16, in_2);
  and and_18 (EN17, decoder_1_out17, in_2);
  and and_19 (EN18, decoder_1_out18, in_2);
  and and_20 (EN19, decoder_1_out19, in_2);
  and and_21 (EN20, decoder_1_out20, in_2);
  and and_22 (EN21, decoder_1_out21, in_2);
  and and_23 (EN22, decoder_1_out22, in_2);
  and and_24 (EN23, decoder_1_out23, in_2);
  and and_25 (EN24, decoder_1_out24, in_2);
  and and_26 (EN25, decoder_1_out25, in_2);
  and and_27 (EN26, decoder_1_out26, in_2);
  and and_28 (EN27, decoder_1_out27, in_2);
  and and_29 (EN28, decoder_1_out28, in_2);
  and and_30 (EN29, decoder_1_out29, in_2);
  and and_31 (EN30, decoder_1_out30, in_2);
  and and_32 (EN31, decoder_1_out31, in_2);
  Register #(.width(32)) register_1 (.D({32{1'b0}}), .en(EN0), .Q(O0), .clk(in_1), .clr(in_7));
  Register #(.width(32)) register_2 (.D(in_6), .en(EN8), .Q(O8), .clk(in_1), .clr(in_7));
  Register #(.width(32)) register_3 (.D(in_6), .en(EN16), .Q(O16), .clk(in_1), .clr(in_7));
  Register #(.width(32)) register_4 (.D(in_6), .en(EN24), .Q(O24), .clk(in_1), .clr(in_7));
  Register #(.width(32)) register_5 (.D(in_6), .en(EN1), .Q(O1), .clk(in_1), .clr(in_7));
  Register #(.width(32)) register_6 (.D(in_6), .en(EN9), .Q(O9), .clk(in_1), .clr(in_7));
  Register #(.width(32)) register_7 (.D(in_6), .en(EN17), .Q(O17), .clk(in_1), .clr(in_7));
  Register #(.width(32)) register_8 (.D(in_6), .en(EN25), .Q(O25), .clk(in_1), .clr(in_7));
  Register #(.width(32)) register_9 (.D(in_6), .en(EN2), .Q(O2), .clk(in_1), .clr(in_7));
  Register #(.width(32)) register_10 (.D(in_6), .en(EN10), .Q(O10), .clk(in_1), .clr(in_7));
  Register #(.width(32)) register_11 (.D(in_6), .en(EN18), .Q(O18), .clk(in_1), .clr(in_7));
  Register #(.width(32)) register_12 (.D(in_6), .en(EN26), .Q(O26), .clk(in_1), .clr(in_7));
  Multiplexer #(.select(5), .width(32)) multiplexer_1 (
    .in0(O0), .in1(O1), .in2(O2), .in3(O3), .in4(O4), .in5(O5), .in6(O6), .in7(O7), .in8(O8), .in9(O9),
    .in10(O10), .in11(O11), .in12(O12), .in13(O13), .in14(O14), .in15(O15), .in16(O16), .in17(O17),
    .in18(O18), .in19(O19), .in20(O20), .in21(O21), .in22(O22), .in23(O23), .in24(O24), .in25(O25),
    .in26(O26), .in27(O27), .in28(O28), .in29(O29), .in30(O30), .in31(O31), .out(out_8), .sel(in_3));  // open: en
  Register #(.width(32)) register_13 (.D(in_6), .en(EN3), .Q(O3), .clk(in_1), .clr(in_7));
  Register #(.width(32)) register_14 (.D(in_6), .en(EN11), .Q(O11), .clk(in_1), .clr(in_7));
  Register #(.width(32)) register_15 (.D(in_6), .en(EN19), .Q(O19), .clk(in_1), .clr(in_7));
  Register #(.width(32)) register_16 (.D(in_6), .en(EN27), .Q(O27), .clk(in_1), .clr(in_7));
  Register #(.width(32)) register_17 (.D(in_6), .en(EN4), .Q(O4), .clk(in_1), .clr(in_7));
  Register #(.width(32)) register_18 (.D(in_6), .en(EN12), .Q(O12), .clk(in_1), .clr(in_7));
  Register #(.width(32)) register_19 (.D(in_6), .en(EN20), .Q(O20), .clk(in_1), .clr(in_7));
  Register #(.width(32)) register_20 (.D(in_6), .en(EN28), .Q(O28), .clk(in_1), .clr(in_7));
  Register #(.width(32)) register_21 (.D(in_6), .en(EN5), .Q(O5), .clk(in_1), .clr(in_7));
  Register #(.width(32)) register_22 (.D(in_6), .en(EN13), .Q(O13), .clk(in_1), .clr(in_7));
  Register #(.width(32)) register_23 (.D(in_6), .en(EN21), .Q(O21), .clk(in_1), .clr(in_7));
  Register #(.width(32)) register_24 (.D(in_6), .en(EN29), .Q(O29), .clk(in_1), .clr(in_7));
  Register #(.width(32)) register_25 (.D(in_6), .en(EN6), .Q(O6), .clk(in_1), .clr(in_7));
  Register #(.width(32)) register_26 (.D(in_6), .en(EN14), .Q(O14), .clk(in_1), .clr(in_7));
  Register #(.width(32)) register_27 (.D(in_6), .en(EN22), .Q(O22), .clk(in_1), .clr(in_7));
  Register #(.width(32)) register_28 (.D(in_6), .en(EN30), .Q(O30), .clk(in_1), .clr(in_7));
  Multiplexer #(.select(5), .width(32)) multiplexer_2 (
    .in0(O0), .in1(O1), .in2(O2), .in3(O3), .in4(O4), .in5(O5), .in6(O6), .in7(O7), .in8(O8), .in9(O9),
    .in10(O10), .in11(O11), .in12(O12), .in13(O13), .in14(O14), .in15(O15), .in16(O16), .in17(O17),
    .in18(O18), .in19(O19), .in20(O20), .in21(O21), .in22(O22), .in23(O23), .in24(O24), .in25(O25),
    .in26(O26), .in27(O27), .in28(O28), .in29(O29), .in30(O30), .in31(O31), .out(out_9), .sel(in_4));  // open: en
  Register #(.width(32)) register_29 (.D(in_6), .en(EN7), .Q(O7), .clk(in_1), .clr(in_7));
  Register #(.width(32)) register_30 (.D(in_6), .en(EN15), .Q(O15), .clk(in_1), .clr(in_7));
  Register #(.width(32)) register_31 (.D(in_6), .en(EN23), .Q(O23), .clk(in_1), .clr(in_7));
  Register #(.width(32)) register_32 (.D(in_6), .en(EN31), .Q(O31), .clk(in_1), .clr(in_7));

  // Other names for the same wires on the sheet: A1[4:0] = in_3; A2[4:0] = in_4; A3[4:0] = in_5; clk = in_1;
  //   RD1[31:0] = out_8; RD2[31:0] = out_9; reset = in_7; WD[31:0] = in_6; we = in_2
endmodule

module DM (
  input  in_1,
  input  [4:0] Addr,
  input  MemWrite,
  input  reset,
  input  [31:0] WD,
  output [31:0] RD
);

  RAM #(.addrWidth(5), .dataWidth(32), .bus("separate")) ram_1 (
    .addr(Addr), .din(WD), .data(RD), .str(MemWrite), .clk(in_1), .clr(reset));  // open: sel, ld

  // Other names for the same wires on the sheet: clk = in_1
endmodule

module NPC (
  input  [31:0] PC,
  input  [25:0] in_2,
  input  [31:0] in_3,
  input  [31:0] in_4,
  input  [1:0] nPC_sel,
  input  in_6,
  output [31:0] NPC
);

  wire [31:0] b, b_t, PC_4, shifter_1_out;

  Adder #(.width(32)) adder_1 (.a(PC), .b(32'h4), .out(PC_4));  // open: cin, cout
  Shifter #(.width(32)) shifter_1 (.in(in_3), .\dist (5'b00010), .out(shifter_1_out));
  Adder #(.width(32)) adder_2 (.a(shifter_1_out), .b(PC_4), .out(b_t));  // open: cin, cout
  Multiplexer #(.width(32), .enable("false")) multiplexer_1 (.in0(PC_4), .in1(b_t), .out(b), .sel(in_6));
  Multiplexer #(.select(2), .width(32), .enable("false")) multiplexer_2 (
    .in0(PC_4), .in1(b), .in2({PC[31:28], in_2, 2'b00}), .in3(in_4), .out(NPC), .sel(nPC_sel));

  // Other names for the same wires on the sheet: EXT_imm16[31:0] = in_3; GPR_rs[31:0] = in_4; isZero = in_6;
  //   imm26[25:0] = in_2; j[31:2] = {PC[31:28], in_2}
endmodule
